// Logisim project 2201CS04_cs227_project.circ as structural Verilog: 19 circuits, main circuit mod60
module CLOCK (
  input  DATE_Reset,
  input  MONTH_Reset,
  input  HOUR_Reset,
  input  MINUTE_Reset,
  input  SECOND_Reset,
  input  D_N__Reset,
  input  DAY_Reset
);

  wire _30, _31, am_pm_1_pm, CLOCK_START_out, comparator_1_eq, comparator_2_eq, d1, d2, d3, d4, d5, d6, d7,
       d8, d9, d10, d11, d12, d13, d14, d15, d16, d17, d18, d19, d20, d21, d22, d23, d24, d25, d26, d27, d28,
       d29, d30, d31, decoder_1_out0, decoder_1_out1, decoder_2_out0, decoder_2_out1, FR, m1, m2, m3, m4, m5,
       m6, m7, m8, m9, m10, m11, m12, m28, m30, m31, MO, multiplexer_2_out, multiplexer_3_out,
       multiplexer_4_out, multiplexer_5_out, multiplexer_8_out, not_1_out, not_2_out, not_3_out, not_4_out,
       not_5_out, SA, SU, TH, TU, WE;
  wire [3:0] ht, hu, mod12count_1_o_p, mt, mu, st, su_t;
  wire [4:0] mod28_reset1_1_output, mod30_reset1_1_output, mod31_reset1_1_output, multiplexer_6_out;
  wire [6:0] _0, _1, _2, _3, _4;
  wire [7:0] multiplexer_1_out;

  AM_PM am_pm_1 (.in_1(multiplexer_1_out), .PM(am_pm_1_pm));  // open: AM
  Multiplexer #(.width(8)) multiplexer_1 (
    .in0({ht, hu}), .in1(8'h12), .out(multiplexer_1_out), .sel(D_N__Reset));  // open: en
  A_P_LED_select a_p_led_select_1 (.Slect(am_pm_1_pm), .out_2(_4), .out_3(_3), .out_4(_2), .out_5(_1), .out_6(_0));
  not not_1 (not_1_out, DAY_Reset);
  Hex_Digit_Display hex_digit_display_1 (.value(hu));  // open: dp
  Hex_Digit_Display hex_digit_display_2 (.value(ht));  // open: dp
  mod12_1_12 mod12_1_12_1 (.clock(multiplexer_2_out), .unitPlace(hu), ._10thPlace(ht));  // open: Reset
  Multiplexer multiplexer_2 (
    .in0(comparator_1_eq), .in1(not_2_out), .out(multiplexer_2_out), .sel(HOUR_Reset));  // open: en
  Multiplexer multiplexer_3 (.in0(am_pm_1_pm), .in1(not_1_out), .out(multiplexer_3_out), .sel(DAY_Reset));  // open: en
  Hex_Digit_Display hex_digit_display_3 (.value(mt));  // open: dp
  mod60 mod60_1 (.clock(multiplexer_4_out), .mod9(mu), .mod6(mt));  // open: Reset
  not not_2 (not_2_out, HOUR_Reset);
  day day_1 (
    .clk(multiplexer_3_out), .out_3(SU), .out_4(MO), .out_5(TU), .out_6(WE), .out_7(TH), .out_8(FR),
    .out_9(SA));  // open: reset
  Hex_Digit_Display hex_digit_display_4 (.value(mu));  // open: dp
  Comparator #(.width(4), .mode("unsigned")) comparator_1 (.a(mt), .b(4'b0000), .eq(comparator_1_eq));  // open: gt, lt
  Hex_Digit_Display hex_digit_display_5 (.value(st));  // open: dp
  Hex_Digit_Display hex_digit_display_6 (.value(su_t));  // open: dp
  mod60 mod60_2 (.clock(CLOCK_START_out), .Reset(SECOND_Reset), .mod9(su_t), .mod6(st));
  Comparator #(.width(4), .mode("unsigned")) comparator_2 (.a(st), .b(4'b0000), .eq(comparator_2_eq));  // open: gt, lt
  Multiplexer multiplexer_4 (
    .in0(comparator_2_eq), .in1(not_3_out), .out(multiplexer_4_out), .sel(MINUTE_Reset));  // open: en
  Multiplexer multiplexer_5 (.in0(am_pm_1_pm), .in1(not_4_out), .out(multiplexer_5_out), .sel(DATE_Reset));  // open: en
  MOD31_reset1 mod31_reset1_1 (.clock(multiplexer_5_out), .reset(m31), .\output (mod31_reset1_1_output));
  MOD30_reset1 mod30_reset1_1 (.clock(multiplexer_5_out), .reset(m30), .\output (mod30_reset1_1_output));
  MOD28_reset1 mod28_reset1_1 (.clock(multiplexer_5_out), .reset(m28), .\output (mod28_reset1_1_output));
  DotMatrix dotmatrix_1 (.col0(_4), .col1(_3), .col2(_2), .col3(_1), .col4(_0));
  not not_3 (not_3_out, MINUTE_Reset);
  not not_4 (not_4_out, DATE_Reset);
  Multiplexer #(.select(2), .width(5)) multiplexer_6 (
    .in0(mod31_reset1_1_output), .in1(mod30_reset1_1_output), .in2(mod28_reset1_1_output),
    .out(multiplexer_6_out), .sel({m2, _30}));  // open: in3, en
  DotMatrix dotmatrix_2 (.col0({7{1'b1}}), .col1(7'b0011000), .col2(7'b0001100), .col3(7'b0011000), .col4({7{1'b1}}));
  Clock CLOCK_START (.out(CLOCK_START_out));
  Decoder #(.select(5)) decoder_1 (
    .out0(decoder_1_out0), .out1(decoder_1_out1), .out2(d2), .out3(d3), .out4(d4), .out5(d5), .out6(d6),
    .out7(d7), .out8(d8), .out9(d9), .out10(d10), .out11(d11), .out12(d12), .out13(d13), .out14(d14),
    .out15(d15), .out16(d16), .out17(d17), .out18(d18), .out19(d19), .out20(d20), .out21(d21), .out22(d22),
    .out23(d23), .out24(d24), .out25(d25), .out26(d26), .out27(d27), .out28(d28), .out29(d29), .out30(d30),
    .out31(d31), .sel(multiplexer_6_out));  // open: en
  Multiplexer multiplexer_7 (.in0(decoder_1_out1), .in1(decoder_1_out0), .out(d1), .sel(decoder_1_out0));  // open: en
  LED MONDAY (.in(MO));
  LED TUESDAY (.in(TU));
  LED WEDNESDAY (.in(WE));
  LED THURSDAY (.in(TH));
  LED FRIDAY (.in(FR));
  LED SATURDAY (.in(SA));
  LED SUNDAY (.in(SU));
  Multiplexer multiplexer_8 (.in0(d1), .in1(not_5_out), .out(multiplexer_8_out), .sel(MONTH_Reset));  // open: en
  or or_1 (m31, _30, m2);
  or or_2 (m30, _31, m2);
  or or_3 (m28, _30, _31);
  not not_5 (not_5_out, MONTH_Reset);
  Decoder #(.select(4)) decoder_2 (
    .out0(decoder_2_out0), .out1(decoder_2_out1), .out2(m2), .out3(m3), .out4(m4), .out5(m5), .out6(m6),
    .out7(m7), .out8(m8), .out9(m9), .out10(m10), .out11(m11), .out12(m12), .sel(mod12count_1_o_p));  // open: out13, out14, out15, en
  mod12count mod12count_1 (.clk(multiplexer_8_out), .o_p(mod12count_1_o_p));
  LED u__1 (.in(d1));
  LED _11 (.in(d11));
  LED _12 (.in(d12));
  LED u__2 (.in(d2));
  LED u__3 (.in(d3));
  LED _13 (.in(d13));
  LED _14 (.in(d14));
  LED u__4 (.in(d4));
  LED _15 (.in(d15));
  LED _5 (.in(d5));
  LED _16 (.in(d16));
  LED _6 (.in(d6));
  LED _7 (.in(d7));
  LED _17 (.in(d17));
  LED _8 (.in(d8));
  LED _18 (.in(d18));
  LED _19 (.in(d19));
  LED _9 (.in(d9));
  LED _20 (.in(d20));
  LED _10 (.in(d10));
  Multiplexer multiplexer_9 (.in0(decoder_2_out1), .in1(decoder_2_out0), .out(m1), .sel(decoder_2_out0));  // open: en
  or or_4 (_30, m4, m6, m9, m11);
  or or_5 (_31, m1, m3, m5, m7, m8, m10, m12);
  LED _21 (.in(d21));
  LED _22 (.in(d22));
  LED _23 (.in(d23));
  LED _24 (.in(d24));
  LED _25 (.in(d25));
  LED _26 (.in(d26));
  LED _27 (.in(d27));
  LED _28 (.in(d28));
  LED _29 (.in(d29));
  LED u__30 (.in(d30));
  LED u__31 (.in(d31));
  LED JAN (.in(m1));
  LED MARCH (.in(m3));
  LED MAY (.in(m5));
  LED JULY (.in(m7));
  LED SEPT (.in(m9));
  LED NOV (.in(m11));
  LED FEB (.in(m2));
  LED APRIL (.in(m4));
  LED JUNE (.in(m6));
  LED AUG (.in(m8));
  LED OCT (.in(m10));
  LED DEC (.in(m12));

  // Other names for the same wires on the sheet: RA_P = D_N__Reset; RD = DAY_Reset; RDate = DATE_Reset;
  //   RH = HOUR_Reset; RM = MINUTE_Reset; RMonth = MONTH_Reset; RS = SECOND_Reset

  // Notes on the sheet:
  //   Day Module
  //   IIT PATNA B.Tech CSE
  //   HOURS
  //   AM-PM Module
  //   .
  //   .
  //   MINUTES
  //   .
  //   .
  //   SECONDS
  //   Clock Module
  //   Date Module
  //   CS227 Project: Digital Clock & Calender
  //   DAY
  //   CALENDER
  //   Month Module
  //   MONTH
  //   ABHINAY KUMAR
  //   2201CS04
endmodule

module STOPWATCH (
  input  START_PAUSE,
  input  Reset
);

  wire clk_out, comparator_1_eq, comparator_2_eq, multiplexer_1_out;
  wire [3:0] mod12_1__10thplace, mod12_1_unitplace, mod60_1_mod6, mod60_1_mod9, mod60_2_mod6, mod60_2_mod9;

  Clock clk (.out(clk_out));
  Multiplexer multiplexer_1 (.in0(clk_out), .in1(START_PAUSE), .out(multiplexer_1_out), .sel(START_PAUSE));  // open: en
  Hex_Digit_Display hex_digit_display_1 (.value(mod12_1__10thplace));  // open: dp
  Hex_Digit_Display hex_digit_display_2 (.value(mod12_1_unitplace));  // open: dp
  mod12 mod12_1 (
    .clock(comparator_1_eq), .Reset(Reset), .unitPlace(mod12_1_unitplace), ._10thPlace(mod12_1__10thplace));
  mod60 mod60_1 (.clock(comparator_2_eq), .Reset(Reset), .mod9(mod60_1_mod9), .mod6(mod60_1_mod6));
  Hex_Digit_Display hex_digit_display_3 (.value(mod60_1_mod9));  // open: dp
  Hex_Digit_Display hex_digit_display_4 (.value(mod60_1_mod6));  // open: dp
  Comparator #(.width(4), .mode("unsigned")) comparator_1 (
    .a(mod60_1_mod6), .b(4'b0000), .eq(comparator_1_eq));  // open: gt, lt
  Hex_Digit_Display hex_digit_display_5 (.value(mod60_2_mod6));  // open: dp
  mod60 mod60_2 (.clock(multiplexer_1_out), .Reset(Reset), .mod9(mod60_2_mod9), .mod6(mod60_2_mod6));
  Comparator #(.width(4), .mode("unsigned")) comparator_2 (
    .a(mod60_2_mod6), .b(4'b0000), .eq(comparator_2_eq));  // open: gt, lt
  Hex_Digit_Display hex_digit_display_6 (.value(mod60_2_mod9));  // open: dp

  // Notes on the sheet:
  //   HOURS
  //   MINUTES
  //   SECONDS
endmodule

module \initial  (
  input  HOUR_Reset,
  input  MINUTE_Reset,
  input  SECOND_Reset,
  input  D_N__Reset,
  input  DAY_Reset
);

  wire am_pm_1_pm, CLOCK_START_out, comparator_1_eq, comparator_2_eq, day_1_out_3, day_1_out_4, day_1_out_5,
       day_1_out_6, day_1_out_7, day_1_out_8, day_1_out_9, multiplexer_1_out, multiplexer_3_out,
       multiplexer_4_out, not_1_out, not_2_out, not_3_out;
  wire [3:0] mod12_1_12_1__10thplace, mod12_1_12_1_unitplace, mod60_1_mod6, mod60_1_mod9, mod60_2_mod6,
       mod60_2_mod9;
  wire [6:0] _0, _1, _2, _3, _4;
  wire [7:0] multiplexer_2_out;

  AM_PM am_pm_1 (.in_1(multiplexer_2_out), .PM(am_pm_1_pm));  // open: AM
  Clock CLOCK_START (.out(CLOCK_START_out));
  mod12_1_12 mod12_1_12_1 (
    .clock(multiplexer_1_out), .unitPlace(mod12_1_12_1_unitplace), ._10thPlace(mod12_1_12_1__10thplace));  // open: Reset
  Multiplexer multiplexer_1 (
    .in0(comparator_1_eq), .in1(not_1_out), .out(multiplexer_1_out), .sel(HOUR_Reset));  // open: en
  Multiplexer #(.width(8)) multiplexer_2 (
    .in0({mod12_1_12_1__10thplace, mod12_1_12_1_unitplace}), .in1(8'h12), .out(multiplexer_2_out),
    .sel(D_N__Reset));  // open: en
  A_P_LED_select a_p_led_select_1 (.Slect(am_pm_1_pm), .out_2(_4), .out_3(_3), .out_4(_2), .out_5(_1), .out_6(_0));
  Hex_Digit_Display hex_digit_display_1 (.value(mod12_1_12_1__10thplace));  // open: dp
  Hex_Digit_Display hex_digit_display_2 (.value(mod12_1_12_1_unitplace));  // open: dp
  not not_1 (not_1_out, HOUR_Reset);
  Hex_Digit_Display hex_digit_display_3 (.value(mod60_1_mod6));  // open: dp
  mod60 mod60_1 (.clock(multiplexer_3_out), .mod9(mod60_1_mod9), .mod6(mod60_1_mod6));  // open: Reset
  Hex_Digit_Display hex_digit_display_4 (.value(mod60_1_mod9));  // open: dp
  mod60 mod60_2 (.clock(CLOCK_START_out), .Reset(SECOND_Reset), .mod9(mod60_2_mod9), .mod6(mod60_2_mod6));
  Comparator #(.width(4), .mode("unsigned")) comparator_1 (
    .a(mod60_1_mod6), .b(4'b0000), .eq(comparator_1_eq));  // open: gt, lt
  Hex_Digit_Display hex_digit_display_5 (.value(mod60_2_mod9));  // open: dp
  Hex_Digit_Display hex_digit_display_6 (.value(mod60_2_mod6));  // open: dp
  Comparator #(.width(4), .mode("unsigned")) comparator_2 (
    .a(mod60_2_mod6), .b(4'b0000), .eq(comparator_2_eq));  // open: gt, lt
  Multiplexer multiplexer_3 (
    .in0(comparator_2_eq), .in1(not_2_out), .out(multiplexer_3_out), .sel(MINUTE_Reset));  // open: en
  DotMatrix dotmatrix_1 (.col0(_4), .col1(_3), .col2(_2), .col3(_1), .col4(_0));
  not not_2 (not_2_out, MINUTE_Reset);
  DotMatrix dotmatrix_2 (.col0({7{1'b1}}), .col1(7'b0011000), .col2(7'b0001100), .col3(7'b0011000), .col4({7{1'b1}}));
  not not_3 (not_3_out, DAY_Reset);
  LED SUNDAY (.in(day_1_out_3));
  Multiplexer multiplexer_4 (.in0(am_pm_1_pm), .in1(not_3_out), .out(multiplexer_4_out), .sel(DAY_Reset));  // open: en
  LED MONDAY (.in(day_1_out_4));
  day day_1 (
    .clk(multiplexer_4_out), .out_3(day_1_out_3), .out_4(day_1_out_4), .out_5(day_1_out_5),
    .out_6(day_1_out_6), .out_7(day_1_out_7), .out_8(day_1_out_8), .out_9(day_1_out_9));  // open: reset
  LED TUESDAY (.in(day_1_out_5));
  LED WEDNESDAY (.in(day_1_out_6));
  LED THURSDAY (.in(day_1_out_7));
  LED SATURDAY (.in(day_1_out_9));
  LED FRIDAY (.in(day_1_out_8));

  // Other names for the same wires on the sheet: RA_P = D_N__Reset; RD = DAY_Reset; RH = HOUR_Reset;
  //   RM = MINUTE_Reset; RS = SECOND_Reset

  // Notes on the sheet:
  //   HOURS
  //   MINUTES
  //   SECONDS
endmodule

module day (
  input  reset,
  input  clk,
  output out_3,
  output out_4,
  output out_5,
  output out_6,
  output out_7,
  output out_8,
  output out_9
);

  wire [2:0] mod7_1_o_p;

  mod7 mod7_1 (.clock(clk), .reset(reset), .o_p(mod7_1_o_p));
  Decoder #(.select(3)) decoder_1 (
    .out0(out_3), .out1(out_4), .out2(out_5), .out3(out_6), .out4(out_7), .out5(out_8), .out6(out_9),
    .sel(mod7_1_o_p));  // open: out7, en
endmodule

module A_P_LED_select (
  input  Slect,
  output [6:0] out_2,
  output [6:0] out_3,
  output [6:0] out_4,
  output [6:0] out_5,
  output [6:0] out_6
);

  Multiplexer #(.width(7)) multiplexer_1 (.in0({7{1'b1}}), .in1(7'b0000111), .out(out_2), .sel(Slect));  // open: en
  Multiplexer #(.width(7)) multiplexer_2 (.in0(7'b1000100), .in1(7'b0011100), .out(out_3), .sel(Slect));  // open: en
  Multiplexer #(.width(7)) multiplexer_3 (.in0(7'b0101000), .in1(7'b0011100), .out(out_5), .sel(Slect));  // open: en
  Multiplexer #(.width(7)) multiplexer_4 (.in0(7'b1000100), .in1(7'b1100100), .out(out_4), .sel(Slect));  // open: en
  Multiplexer #(.width(7)) multiplexer_5 (.in0(7'b0010000), .in1(7'b0000111), .out(out_6), .sel(Slect));  // open: en
endmodule

module AM_PM (
  input  [7:0] in_1,
  output PM,
  output AM
);

  wire comparator_1_eq;

  Comparator comparator_1 (.a(in_1), .b(8'h12), .eq(comparator_1_eq));  // open: gt, lt
  T_Flip_Flop t_ff_1 (.clk(comparator_1_eq), .T(comparator_1_eq), .Q(PM), .Qn(AM));  // open: preset, reset, en
endmodule

module mod2 (
  input  in_1,
  input  in_2,
  output [1:0] out_3
);

  wire and_1_out, not_1_out, not_2_out;

  not not_1 (not_1_out, out_3[1]);
  not not_2 (not_2_out, out_3[0]);
  and and_1 (and_1_out, not_1_out, not_2_out);
  D_Flip_Flop d_ff_1 (.clk(in_1), .D(1'b0), .Q(out_3[1]), .reset(in_2));  // open: Qn, preset, en
  D_Flip_Flop d_ff_2 (.clk(in_1), .D(and_1_out), .Q(out_3[0]), .reset(in_2));  // open: Qn, preset, en
  Hex_Digit_Display hex_digit_display_1 (.value({2'b00, out_3}));  // open: dp
endmodule

module mod3 (
  input  in_1,
  input  in_2,
  output [1:0] out_3
);

  wire and_1_out, and_2_out, not_1_out, not_2_out, not_3_out;

  not not_1 (not_1_out, out_3[1]);
  not not_2 (not_2_out, out_3[1]);
  not not_3 (not_3_out, out_3[0]);
  and and_1 (and_1_out, not_1_out, out_3[0]);
  and and_2 (and_2_out, not_2_out, not_3_out);
  D_Flip_Flop d_ff_1 (.clk(in_1), .D(and_1_out), .Q(out_3[1]), .reset(in_2));  // open: Qn, preset, en
  D_Flip_Flop d_ff_2 (.clk(in_1), .D(and_2_out), .Q(out_3[0]), .reset(in_2));  // open: Qn, preset, en
  Hex_Digit_Display hex_digit_display_1 (.value({2'b00, out_3}));  // open: dp
endmodule

module mod4 (
  input  clk,
  input  Enable,
  output [3:0] o_p
);

  wire and_1_out, and_2_out, d_ff_1_qn, d_ff_2_qn, or_1_out;

  and and_1 (and_1_out, d_ff_1_qn, o_p[0]);
  and and_2 (and_2_out, o_p[1], d_ff_2_qn);
  or or_1 (or_1_out, and_1_out, and_2_out);
  D_Flip_Flop d_ff_1 (.clk(clk), .D(or_1_out), .Q(o_p[1]), .Qn(d_ff_1_qn), .reset(Enable));  // open: preset, en
  D_Flip_Flop d_ff_2 (.clk(clk), .D(d_ff_2_qn), .Q(o_p[0]), .Qn(d_ff_2_qn), .reset(Enable));  // open: preset, en
  Hex_Digit_Display hex_digit_display_1 (.value({2'b00, o_p[1:0]}));  // open: dp

  assign o_p[3:2] = 2'b00;
endmodule

module mod6 (
  input  in_1,
  input  reset,
  output [2:0] out_3
);

  wire and_1_out, and_2_out, and_3_out, and_4_out, and_5_out, and_6_out, not_1_out, not_2_out, not_3_out,
       not_4_out, not_5_out, not_6_out, not_7_out, not_8_out, not_9_out, not_10_out, not_11_out, or_1_out,
       or_2_out, or_3_out;

  not not_1 (not_1_out, out_3[2]);
  not not_2 (not_2_out, out_3[1]);
  not not_3 (not_3_out, out_3[0]);
  not not_4 (not_4_out, out_3[2]);
  not not_5 (not_5_out, out_3[1]);
  not not_6 (not_6_out, out_3[2]);
  not not_7 (not_7_out, out_3[0]);
  not not_8 (not_8_out, out_3[2]);
  not not_9 (not_9_out, out_3[0]);
  not not_10 (not_10_out, out_3[1]);
  not not_11 (not_11_out, out_3[0]);
  and and_1 (and_1_out, not_1_out, out_3[1], out_3[0]);
  and and_2 (and_2_out, out_3[2], not_2_out, not_3_out);
  and and_3 (and_3_out, not_4_out, not_5_out, out_3[0]);
  and and_4 (and_4_out, not_6_out, out_3[1], not_7_out);
  and and_5 (and_5_out, not_8_out, not_9_out);
  and and_6 (and_6_out, not_10_out, not_11_out);
  or or_1 (or_1_out, and_1_out, and_2_out);
  or or_2 (or_2_out, and_3_out, and_4_out);
  or or_3 (or_3_out, and_5_out, and_6_out);
  D_Flip_Flop d_ff_1 (.clk(in_1), .D(or_1_out), .Q(out_3[2]), .reset(reset));  // open: Qn, preset, en
  D_Flip_Flop d_ff_2 (.clk(in_1), .D(or_2_out), .Q(out_3[1]), .reset(reset));  // open: Qn, preset, en
  D_Flip_Flop d_ff_3 (.clk(in_1), .D(or_3_out), .Q(out_3[0]), .reset(reset));  // open: Qn, preset, en
  Hex_Digit_Display hex_digit_display_1 (.value({1'b0, out_3}));  // open: dp
endmodule

module mod7 (
  input  clock,
  input  reset,
  output [2:0] o_p
);

  wire and_1_out, and_2_out, and_3_out, and_4_out, and_5_out, and_6_out, not_1_out, not_2_out, not_3_out,
       not_4_out, not_5_out, not_6_out, not_7_out, not_8_out, not_9_out, or_1_out, or_2_out, or_3_out;

  not not_1 (not_1_out, o_p[2]);
  not not_2 (not_2_out, o_p[1]);
  not not_3 (not_3_out, o_p[1]);
  not not_4 (not_4_out, o_p[2]);
  not not_5 (not_5_out, o_p[0]);
  not not_6 (not_6_out, o_p[2]);
  not not_7 (not_7_out, o_p[0]);
  not not_8 (not_8_out, o_p[1]);
  not not_9 (not_9_out, o_p[0]);
  and and_1 (and_1_out, not_1_out, o_p[1], o_p[0]);
  and and_2 (and_2_out, o_p[2], not_2_out);
  and and_3 (and_3_out, not_3_out, o_p[0]);
  and and_4 (and_4_out, not_4_out, o_p[1], not_5_out);
  and and_5 (and_5_out, not_6_out, not_7_out);
  and and_6 (and_6_out, not_8_out, not_9_out);
  or or_1 (or_1_out, and_1_out, and_2_out);
  or or_2 (or_2_out, and_3_out, and_4_out);
  or or_3 (or_3_out, and_5_out, and_6_out);
  D_Flip_Flop d_ff_1 (.clk(clock), .D(or_1_out), .Q(o_p[2]), .reset(reset));  // open: Qn, preset, en
  D_Flip_Flop d_ff_2 (.clk(clock), .D(or_2_out), .Q(o_p[1]), .reset(reset));  // open: Qn, preset, en
  D_Flip_Flop d_ff_3 (.clk(clock), .D(or_3_out), .Q(o_p[0]), .reset(reset));  // open: Qn, preset, en
  Hex_Digit_Display hex_digit_display_1 (.value({1'b0, o_p}));  // open: dp
endmodule

module mod10 (
  input  in_1,
  input  reset,
  output [3:0] out_3
);

  wire and_1_out, and_2_out, and_3_out, and_4_out, and_5_out, and_6_out, and_7_out, and_8_out, and_9_out,
       not_1_out, not_2_out, not_3_out, not_4_out, not_5_out, not_6_out, not_7_out, not_8_out, not_9_out,
       not_10_out, not_11_out, not_12_out, not_13_out, not_14_out, not_15_out, not_16_out, not_17_out,
       not_18_out, not_19_out, or_1_out, or_2_out, or_3_out, or_4_out;

  not not_1 (not_1_out, out_3[3]);
  not not_2 (not_2_out, out_3[2]);
  not not_3 (not_3_out, out_3[1]);
  not not_4 (not_4_out, out_3[0]);
  not not_5 (not_5_out, out_3[3]);
  not not_6 (not_6_out, out_3[2]);
  not not_7 (not_7_out, out_3[3]);
  not not_8 (not_8_out, out_3[1]);
  not not_9 (not_9_out, out_3[3]);
  not not_10 (not_10_out, out_3[0]);
  not not_11 (not_11_out, out_3[3]);
  not not_12 (not_12_out, out_3[0]);
  not not_13 (not_13_out, out_3[2]);
  not not_14 (not_14_out, out_3[1]);
  not not_15 (not_15_out, out_3[0]);
  and and_1 (and_1_out, not_1_out, out_3[2], out_3[1], out_3[0]);
  and and_2 (and_2_out, out_3[3], not_2_out, not_3_out, not_4_out);
  and and_3 (and_3_out, not_5_out, not_6_out, out_3[1], out_3[0]);
  not not_16 (not_16_out, out_3[3]);
  and and_4 (and_4_out, not_16_out, out_3[2], not_17_out);
  not not_17 (not_17_out, out_3[1]);
  not not_18 (not_18_out, out_3[3]);
  and and_5 (and_5_out, not_18_out, out_3[2], not_19_out);
  not not_19 (not_19_out, out_3[0]);
  and and_6 (and_6_out, not_7_out, not_8_out, out_3[0]);
  and and_7 (and_7_out, not_9_out, out_3[1], not_10_out);
  and and_8 (and_8_out, not_11_out, not_12_out);
  and and_9 (and_9_out, not_13_out, not_14_out, not_15_out);
  or or_1 (or_1_out, and_1_out, and_2_out);
  or or_2 (or_2_out, and_3_out, and_4_out, and_5_out);
  or or_3 (or_3_out, and_6_out, and_7_out);
  or or_4 (or_4_out, and_8_out, and_9_out);
  D_Flip_Flop d_ff_1 (.clk(in_1), .D(or_1_out), .Q(out_3[3]), .reset(reset));  // open: Qn, preset, en
  D_Flip_Flop d_ff_2 (.clk(in_1), .D(or_2_out), .Q(out_3[2]), .reset(reset));  // open: Qn, preset, en
  D_Flip_Flop d_ff_3 (.clk(in_1), .D(or_3_out), .Q(out_3[1]), .reset(reset));  // open: Qn, preset, en
  D_Flip_Flop d_ff_4 (.clk(in_1), .D(or_4_out), .Q(out_3[0]), .reset(reset));  // open: Qn, preset, en
  Hex_Digit_Display hex_digit_display_1 (.value(out_3));  // open: dp
endmodule

module mod12 (
  input  Reset,
  input  clock,
  output [3:0] unitPlace,
  output [3:0] _10thPlace
);

  wire comparator_1_eq, comparator_2_eq, multiplexer_1_out;

  mod10 mod10_1 (.in_1(clock), .reset(multiplexer_1_out), .out_3(unitPlace));
  Multiplexer multiplexer_1 (
    .in0(Reset), .in1(comparator_2_eq), .out(multiplexer_1_out), .sel(comparator_2_eq));  // open: en
  Comparator #(.width(4), .mode("unsigned")) comparator_1 (
    .a(unitPlace), .b(4'b0000), .eq(comparator_1_eq));  // open: gt, lt
  mod2 mod2_1 (.in_1(comparator_1_eq), .in_2(multiplexer_1_out), .out_3(_10thPlace[1:0]));
  Comparator #(.width(6), .mode("unsigned")) comparator_2 (
    .a({unitPlace, _10thPlace[1:0]}), .b(6'b001001), .eq(comparator_2_eq));  // open: gt, lt
  Hex_Digit_Display hex_digit_display_1 (.value({2'b00, _10thPlace[1:0]}));  // open: dp
  Hex_Digit_Display hex_digit_display_2 (.value(unitPlace));  // open: dp

  assign _10thPlace[3:2] = 2'b00;
endmodule

// 12
module mod12_1_12 (
  input  Reset,
  input  clock,
  output [3:0] unitPlace,
  output [3:0] _10thPlace
);

  wire clock_1_out, comparator_1_eq, comparator_2_eq, comparator_3_eq, multiplexer_1_out, multiplexer_2_out;

  Clock clock_1 (.out(clock_1_out));
  Multiplexer multiplexer_1 (
    .in0(clock), .in1(clock_1_out), .out(multiplexer_1_out), .sel(comparator_3_eq));  // open: en
  mod10 mod10_1 (.in_1(multiplexer_1_out), .reset(multiplexer_2_out), .out_3(unitPlace));
  Comparator #(.width(4), .mode("unsigned")) comparator_1 (
    .a(unitPlace), .b(4'b0000), .eq(comparator_1_eq));  // open: gt, lt
  Multiplexer multiplexer_2 (
    .in0(Reset), .in1(comparator_2_eq), .out(multiplexer_2_out), .sel(comparator_2_eq));  // open: en
  mod2 mod2_1 (.in_1(comparator_1_eq), .in_2(multiplexer_2_out), .out_3(_10thPlace[1:0]));
  Comparator #(.width(6), .mode("unsigned")) comparator_2 (
    .a({unitPlace, _10thPlace[1:0]}), .b(6'b001101), .eq(comparator_2_eq));  // open: gt, lt
  Hex_Digit_Display hex_digit_display_1 (.value(unitPlace));  // open: dp
  Hex_Digit_Display hex_digit_display_2 (.value({2'b00, _10thPlace[1:0]}));  // open: dp
  Comparator comparator_3 (
    .a({2'b00, _10thPlace[1:0], unitPlace}), .b({8{1'b0}}), .eq(comparator_3_eq));  // open: gt, lt

  assign _10thPlace[3:2] = 2'b00;
endmodule

// 60
module mod60 (
  input  Reset,
  input  clock,
  output [3:0] mod9,
  output [3:0] mod6
);

  wire comparator_1_eq;

  mod10 mod10_1 (.in_1(clock), .reset(Reset), .out_3(mod9));
  Comparator #(.width(4), .mode("unsigned")) comparator_1 (
    .a(mod9), .b(4'b0000), .eq(comparator_1_eq));  // open: gt, lt
  mod6 mod6_1 (.in_1(comparator_1_eq), .reset(Reset), .out_3(mod6[2:0]));
  Hex_Digit_Display hex_digit_display_1 (.value({1'b0, mod6[2:0]}));  // open: dp
  Hex_Digit_Display hex_digit_display_2 (.value(mod9));  // open: dp

  assign mod6[3] = 1'b0;
endmodule

module mod12count (
  input  clk,
  output [3:0] o_p
);

  wire and_1_out, and_2_out, and_3_out, and_4_out, and_5_out, and_6_out, and_7_out, and_8_out, and_9_out,
       and_10_out, not_1_out, not_2_out, not_3_out, not_4_out, not_5_out, not_6_out, not_7_out, not_8_out,
       not_9_out, not_10_out, not_11_out, not_12_out, not_13_out, not_14_out, not_15_out, not_16_out,
       or_1_out, or_2_out, or_3_out, or_4_out;

  not not_1 (not_1_out, o_p[3]);
  not not_2 (not_2_out, o_p[2]);
  not not_3 (not_3_out, o_p[2]);
  not not_4 (not_4_out, o_p[3]);
  not not_5 (not_5_out, o_p[1]);
  not not_6 (not_6_out, o_p[3]);
  not not_7 (not_7_out, o_p[0]);
  not not_8 (not_8_out, o_p[3]);
  not not_9 (not_9_out, o_p[1]);
  not not_10 (not_10_out, o_p[2]);
  not not_11 (not_11_out, o_p[1]);
  not not_12 (not_12_out, o_p[3]);
  not not_13 (not_13_out, o_p[0]);
  not not_14 (not_14_out, o_p[2]);
  not not_15 (not_15_out, o_p[0]);
  not not_16 (not_16_out, o_p[0]);
  and and_1 (and_1_out, o_p[3], o_p[2]);
  and and_2 (and_2_out, not_1_out, o_p[2], o_p[1], o_p[0]);
  and and_3 (and_3_out, o_p[3], not_2_out);
  and and_4 (and_4_out, not_3_out, o_p[1], o_p[0]);
  and and_5 (and_5_out, not_4_out, o_p[2], not_5_out);
  and and_6 (and_6_out, not_6_out, o_p[2], not_7_out);
  and and_7 (and_7_out, not_8_out, not_9_out, o_p[0]);
  and and_8 (and_8_out, not_10_out, not_11_out, o_p[0]);
  and and_9 (and_9_out, not_12_out, o_p[1], not_13_out);
  and and_10 (and_10_out, not_14_out, o_p[1], not_15_out);
  or or_1 (or_1_out, not_16_out, and_1_out);
  or or_2 (or_2_out, and_2_out, and_3_out);
  or or_3 (or_3_out, and_4_out, and_5_out, and_6_out);
  or or_4 (or_4_out, and_7_out, and_8_out, and_9_out, and_10_out);
  D_Flip_Flop d_ff_1 (.clk(clk), .D(or_2_out), .Q(o_p[3]));  // open: Qn, preset, en, reset
  D_Flip_Flop d_ff_2 (.clk(clk), .D(or_3_out), .Q(o_p[2]));  // open: Qn, preset, en, reset
  D_Flip_Flop d_ff_3 (.clk(clk), .D(or_4_out), .Q(o_p[1]));  // open: Qn, preset, en, reset
  D_Flip_Flop d_ff_4 (.clk(clk), .D(or_1_out), .Q(o_p[0]));  // open: Qn, preset, en, reset
endmodule

module MOD31_reset1 (
  input  reset,
  input  clock,
  output [4:0] \output 
);

  wire and_1_out, and_2_out, and_3_out, and_4_out, and_5_out, and_6_out, and_7_out, and_8_out, and_9_out,
       and_10_out, and_11_out, and_12_out, and_13_out, and_14_out, and_15_out, multiplexer_1_out,
       multiplexer_2_out, not_2_out, not_3_out, not_4_out, not_5_out, not_6_out, not_7_out, not_8_out,
       not_9_out, not_10_out, not_11_out, not_12_out, not_13_out, not_14_out, not_15_out, not_16_out,
       not_17_out, not_18_out, not_19_out, not_20_out, not_21_out, not_22_out, not_23_out, not_24_out,
       not_25_out, not_26_out, not_27_out, not_28_out, not_29_out, not_30_out, or_1_out, or_2_out, or_3_out,
       or_4_out, or_5_out;
  wire [0:0] not_1_out;

  Multiplexer #(.select(2)) multiplexer_1 (
    .in1(clock), .in2(1'b0), .out(multiplexer_1_out), .sel({reset, not_1_out[0]}));  // open: in0, in3, en
  not not_1 (not_1_out[0], reset);
  Multiplexer multiplexer_2 (
    .in0(multiplexer_1_out), .in1(not_1_out[0]), .out(multiplexer_2_out), .sel(reset));  // open: en
  not not_2 (not_2_out, reset);
  not not_3 (not_3_out, \output [4]);
  not not_4 (not_4_out, reset);
  not not_5 (not_5_out, \output [3]);
  not not_6 (not_6_out, reset);
  not not_7 (not_7_out, \output [2]);
  not not_8 (not_8_out, reset);
  not not_9 (not_9_out, \output [1]);
  not not_10 (not_10_out, reset);
  not not_11 (not_11_out, \output [0]);
  not not_12 (not_12_out, reset);
  not not_13 (not_13_out, \output [3]);
  not not_14 (not_14_out, reset);
  not not_15 (not_15_out, \output [2]);
  not not_16 (not_16_out, reset);
  not not_17 (not_17_out, \output [1]);
  not not_18 (not_18_out, reset);
  not not_19 (not_19_out, \output [0]);
  not not_20 (not_20_out, reset);
  not not_21 (not_21_out, \output [2]);
  not not_22 (not_22_out, reset);
  not not_23 (not_23_out, \output [1]);
  not not_24 (not_24_out, reset);
  not not_25 (not_25_out, \output [0]);
  not not_26 (not_26_out, reset);
  not not_27 (not_27_out, \output [1]);
  not not_28 (not_28_out, reset);
  not not_29 (not_29_out, \output [0]);
  not not_30 (not_30_out, \output [0]);
  and and_1 (and_1_out, \output [4], \output [3], \output [2], \output [1]);
  and and_2 (and_2_out, not_2_out, not_3_out, \output [3], \output [2], \output [1], \output [0]);
  and and_3 (and_3_out, not_4_out, \output [4], not_5_out);
  and and_4 (and_4_out, not_6_out, \output [4], not_7_out);
  and and_5 (and_5_out, not_8_out, \output [4], not_9_out);
  and and_6 (and_6_out, not_10_out, \output [4], not_11_out);
  and and_7 (and_7_out, not_12_out, not_13_out, \output [2], \output [1], \output [0]);
  and and_8 (and_8_out, not_14_out, \output [3], not_15_out);
  and and_9 (and_9_out, not_16_out, \output [3], not_17_out);
  and and_10 (and_10_out, not_18_out, \output [3], not_19_out);
  and and_11 (and_11_out, not_20_out, not_21_out, \output [1], \output [0]);
  and and_12 (and_12_out, not_22_out, \output [2], not_23_out);
  and and_13 (and_13_out, not_24_out, \output [2], not_25_out);
  and and_14 (and_14_out, not_26_out, not_27_out, \output [0]);
  and and_15 (and_15_out, not_28_out, \output [1], not_29_out);
  or or_1 (or_1_out, not_30_out, and_1_out, reset);
  or or_2 (or_2_out, and_2_out, and_3_out, and_4_out, and_5_out, and_6_out);
  or or_3 (or_3_out, and_7_out, and_8_out, and_9_out, and_10_out);
  or or_4 (or_4_out, and_11_out, and_12_out, and_13_out);
  or or_5 (or_5_out, and_14_out, and_15_out);
  D_Flip_Flop d_ff_1 (.clk(multiplexer_2_out), .D(or_2_out), .Q(\output [4]));  // open: Qn, preset, en, reset
  D_Flip_Flop d_ff_2 (.clk(multiplexer_2_out), .D(or_3_out), .Q(\output [3]));  // open: Qn, preset, en, reset
  D_Flip_Flop d_ff_3 (.clk(multiplexer_2_out), .D(or_4_out), .Q(\output [2]));  // open: Qn, preset, en, reset
  D_Flip_Flop d_ff_4 (.clk(multiplexer_2_out), .D(or_5_out), .Q(\output [1]));  // open: Qn, preset, en, reset
  D_Flip_Flop d_ff_5 (.clk(multiplexer_2_out), .D(or_1_out), .Q(\output [0]));  // open: Qn, preset, en, reset

  // Other names for the same wires on the sheet: q0 = \output [0]; q1 = \output [1]; q2 = \output [2];
  //   q3 = \output [3]; q4 = \output [4]
endmodule

module MOD30_reset1 (
  input  reset,
  input  clock,
  output [4:0] \output 
);

  wire and_1_out, and_2_out, and_3_out, and_4_out, and_5_out, and_6_out, and_7_out, and_8_out, and_9_out,
       and_10_out, and_11_out, and_12_out, and_13_out, and_14_out, and_15_out, and_16_out, and_17_out,
       multiplexer_1_out, multiplexer_2_out, not_2_out, not_3_out, not_4_out, not_5_out, not_6_out,
       not_7_out, not_8_out, not_9_out, not_10_out, not_11_out, not_12_out, not_13_out, not_14_out,
       not_15_out, not_16_out, not_17_out, not_18_out, not_19_out, not_20_out, not_21_out, not_22_out,
       not_23_out, not_24_out, not_25_out, not_26_out, not_27_out, not_28_out, not_29_out, not_30_out,
       not_31_out, not_32_out, not_33_out, not_34_out, not_35_out, not_36_out, not_37_out, not_38_out,
       not_39_out, not_40_out, or_1_out, or_2_out, or_3_out, or_4_out, or_5_out;
  wire [0:0] not_1_out;

  Multiplexer #(.select(2)) multiplexer_1 (
    .in1(clock), .in2(1'b0), .out(multiplexer_1_out), .sel({reset, not_1_out[0]}));  // open: in0, in3, en
  not not_1 (not_1_out[0], reset);
  Multiplexer multiplexer_2 (
    .in0(multiplexer_1_out), .in1(not_1_out[0]), .out(multiplexer_2_out), .sel(reset));  // open: en
  not not_2 (not_2_out, reset);
  not not_3 (not_3_out, \output [4]);
  not not_4 (not_4_out, reset);
  not not_5 (not_5_out, \output [3]);
  not not_6 (not_6_out, reset);
  not not_7 (not_7_out, \output [2]);
  not not_8 (not_8_out, reset);
  not not_9 (not_9_out, \output [1]);
  not not_10 (not_10_out, reset);
  not not_11 (not_11_out, \output [3]);
  not not_12 (not_12_out, reset);
  not not_13 (not_13_out, \output [4]);
  not not_14 (not_14_out, \output [0]);
  not not_15 (not_15_out, reset);
  not not_16 (not_16_out, \output [2]);
  not not_17 (not_17_out, reset);
  not not_18 (not_18_out, \output [1]);
  not not_19 (not_19_out, reset);
  not not_20 (not_20_out, \output [2]);
  not not_21 (not_21_out, reset);
  not not_22 (not_22_out, \output [4]);
  not not_23 (not_23_out, \output [0]);
  not not_24 (not_24_out, reset);
  not not_25 (not_25_out, \output [3]);
  not not_26 (not_26_out, \output [0]);
  not not_27 (not_27_out, reset);
  not not_28 (not_28_out, \output [1]);
  not not_29 (not_29_out, reset);
  not not_30 (not_30_out, \output [1]);
  not not_31 (not_31_out, reset);
  not not_32 (not_32_out, \output [4]);
  not not_33 (not_33_out, \output [0]);
  not not_34 (not_34_out, reset);
  not not_35 (not_35_out, \output [3]);
  not not_36 (not_36_out, \output [0]);
  not not_37 (not_37_out, reset);
  not not_38 (not_38_out, \output [2]);
  not not_39 (not_39_out, \output [0]);
  not not_40 (not_40_out, \output [0]);
  and and_1 (and_1_out, \output [4], \output [3], \output [2], \output [1]);
  and and_2 (and_2_out, not_2_out, not_3_out, \output [3], \output [2], \output [1], \output [0]);
  and and_3 (and_3_out, not_4_out, \output [4], not_5_out);
  and and_4 (and_4_out, not_6_out, \output [4], not_7_out);
  and and_5 (and_5_out, not_8_out, \output [4], not_9_out);
  and and_6 (and_6_out, not_10_out, not_11_out, \output [2], \output [1], \output [0]);
  and and_7 (and_7_out, not_12_out, not_13_out, \output [3], not_14_out);
  and and_8 (and_8_out, not_15_out, \output [3], not_16_out);
  and and_9 (and_9_out, not_17_out, \output [3], not_18_out);
  and and_10 (and_10_out, not_19_out, not_20_out, \output [1], \output [0]);
  and and_11 (and_11_out, not_21_out, not_22_out, \output [2], not_23_out);
  and and_12 (and_12_out, not_24_out, not_25_out, \output [2], not_26_out);
  and and_13 (and_13_out, not_27_out, \output [2], not_28_out);
  and and_14 (and_14_out, not_29_out, not_30_out, \output [0]);
  and and_15 (and_15_out, not_31_out, not_32_out, \output [1], not_33_out);
  and and_16 (and_16_out, not_34_out, not_35_out, \output [1], not_36_out);
  and and_17 (and_17_out, not_37_out, not_38_out, \output [1], not_39_out);
  or or_1 (or_1_out, not_40_out, and_1_out, reset);
  or or_2 (or_2_out, and_2_out, and_3_out, and_4_out, and_5_out);
  or or_3 (or_3_out, and_6_out, and_7_out, and_8_out, and_9_out);
  or or_4 (or_4_out, and_10_out, and_11_out, and_12_out, and_13_out);
  or or_5 (or_5_out, and_14_out, and_15_out, and_16_out, and_17_out);
  D_Flip_Flop d_ff_1 (.clk(multiplexer_2_out), .D(or_2_out), .Q(\output [4]));  // open: Qn, preset, en, reset
  D_Flip_Flop d_ff_2 (.clk(multiplexer_2_out), .D(or_3_out), .Q(\output [3]));  // open: Qn, preset, en, reset
  D_Flip_Flop d_ff_3 (.clk(multiplexer_2_out), .D(or_4_out), .Q(\output [2]));  // open: Qn, preset, en, reset
  D_Flip_Flop d_ff_4 (.clk(multiplexer_2_out), .D(or_5_out), .Q(\output [1]));  // open: Qn, preset, en, reset
  D_Flip_Flop d_ff_5 (.clk(multiplexer_2_out), .D(or_1_out), .Q(\output [0]));  // open: Qn, preset, en, reset

  // Other names for the same wires on the sheet: q0 = \output [0]; q1 = \output [1]; q2 = \output [2];
  //   q3 = \output [3]; q4 = \output [4]
endmodule

module MOD28_reset1 (
  input  reset,
  input  clock,
  output [4:0] \output 
);

  wire and_1_out, and_2_out, and_3_out, and_4_out, and_5_out, and_6_out, and_7_out, and_8_out, and_9_out,
       and_10_out, and_11_out, and_12_out, and_13_out, and_14_out, and_15_out, and_16_out, and_17_out,
       and_18_out, and_19_out, multiplexer_1_out, multiplexer_2_out, not_2_out, not_3_out, not_4_out,
       not_5_out, not_6_out, not_7_out, not_8_out, not_9_out, not_10_out, not_11_out, not_12_out, not_13_out,
       not_14_out, not_15_out, not_16_out, not_17_out, not_18_out, not_19_out, not_20_out, not_21_out,
       not_22_out, not_23_out, not_24_out, not_25_out, not_26_out, not_27_out, not_28_out, not_29_out,
       not_30_out, not_31_out, not_32_out, not_33_out, not_34_out, not_35_out, not_36_out, not_37_out,
       not_38_out, not_39_out, not_40_out, not_41_out, not_42_out, not_43_out, not_44_out, not_45_out,
       not_46_out, not_47_out, not_48_out, not_49_out, not_50_out, or_1_out, or_2_out, or_3_out, or_4_out,
       or_5_out;
  wire [0:0] not_1_out;

  Multiplexer #(.select(2)) multiplexer_1 (
    .in1(clock), .in2(1'b0), .out(multiplexer_1_out), .sel({reset, not_1_out[0]}));  // open: in0, in3, en
  not not_1 (not_1_out[0], reset);
  Multiplexer multiplexer_2 (
    .in0(multiplexer_1_out), .in1(not_1_out[0]), .out(multiplexer_2_out), .sel(reset));  // open: en
  not not_2 (not_2_out, reset);
  not not_3 (not_3_out, \output [4]);
  not not_4 (not_4_out, reset);
  not not_5 (not_5_out, \output [3]);
  not not_6 (not_6_out, reset);
  not not_7 (not_7_out, \output [2]);
  not not_8 (not_8_out, reset);
  not not_9 (not_9_out, \output [3]);
  not not_10 (not_10_out, reset);
  not not_11 (not_11_out, \output [4]);
  not not_12 (not_12_out, \output [1]);
  not not_13 (not_13_out, reset);
  not not_14 (not_14_out, \output [4]);
  not not_15 (not_15_out, \output [0]);
  not not_16 (not_16_out, reset);
  not not_17 (not_17_out, \output [2]);
  not not_18 (not_18_out, reset);
  not not_19 (not_19_out, \output [2]);
  not not_20 (not_20_out, reset);
  not not_21 (not_21_out, \output [4]);
  not not_22 (not_22_out, \output [1]);
  not not_23 (not_23_out, reset);
  not not_24 (not_24_out, \output [4]);
  not not_25 (not_25_out, \output [0]);
  not not_26 (not_26_out, reset);
  not not_27 (not_27_out, \output [3]);
  not not_28 (not_28_out, \output [1]);
  not not_29 (not_29_out, reset);
  not not_30 (not_30_out, \output [3]);
  not not_31 (not_31_out, \output [0]);
  not not_32 (not_32_out, reset);
  not not_33 (not_33_out, \output [4]);
  not not_34 (not_34_out, \output [1]);
  not not_35 (not_35_out, reset);
  not not_36 (not_36_out, \output [3]);
  not not_37 (not_37_out, \output [1]);
  not not_38 (not_38_out, reset);
  not not_39 (not_39_out, \output [2]);
  not not_40 (not_40_out, \output [1]);
  not not_41 (not_41_out, reset);
  not not_42 (not_42_out, \output [4]);
  not not_43 (not_43_out, \output [0]);
  not not_44 (not_44_out, reset);
  not not_45 (not_45_out, \output [3]);
  not not_46 (not_46_out, \output [0]);
  not not_47 (not_47_out, reset);
  not not_48 (not_48_out, \output [2]);
  not not_49 (not_49_out, \output [0]);
  not not_50 (not_50_out, \output [0]);
  and and_1 (and_1_out, \output [4], \output [3], \output [2]);
  and and_2 (and_2_out, not_2_out, not_3_out, \output [3], \output [2], \output [1], \output [0]);
  and and_3 (and_3_out, not_4_out, \output [4], not_5_out);
  and and_4 (and_4_out, not_6_out, \output [4], not_7_out);
  and and_5 (and_5_out, not_8_out, not_9_out, \output [2], \output [1], \output [0]);
  and and_6 (and_6_out, not_10_out, not_11_out, \output [3], not_12_out);
  and and_7 (and_7_out, not_13_out, not_14_out, \output [3], not_15_out);
  and and_8 (and_8_out, not_16_out, \output [3], not_17_out);
  and and_9 (and_9_out, not_18_out, not_19_out, \output [1], \output [0]);
  and and_10 (and_10_out, not_20_out, not_21_out, \output [2], not_22_out);
  and and_11 (and_11_out, not_23_out, not_24_out, \output [2], not_25_out);
  and and_12 (and_12_out, not_26_out, not_27_out, \output [2], not_28_out);
  and and_13 (and_13_out, not_29_out, not_30_out, \output [2], not_31_out);
  and and_14 (and_14_out, not_32_out, not_33_out, not_34_out, \output [0]);
  and and_15 (and_15_out, not_35_out, not_36_out, not_37_out, \output [0]);
  and and_16 (and_16_out, not_38_out, not_39_out, not_40_out, \output [0]);
  and and_17 (and_17_out, not_41_out, not_42_out, \output [1], not_43_out);
  and and_18 (and_18_out, not_44_out, not_45_out, \output [1], not_46_out);
  and and_19 (and_19_out, not_47_out, not_48_out, \output [1], not_49_out);
  or or_1 (or_1_out, not_50_out, and_1_out, reset);
  or or_2 (or_2_out, and_2_out, and_3_out, and_4_out);
  or or_3 (or_3_out, and_5_out, and_6_out, and_7_out, and_8_out);
  or or_4 (or_4_out, and_9_out, and_10_out, and_11_out, and_12_out, and_13_out);
  or or_5 (or_5_out, and_14_out, and_15_out, and_16_out, and_17_out, and_18_out, and_19_out);
  D_Flip_Flop d_ff_1 (.clk(multiplexer_2_out), .D(or_2_out), .Q(\output [4]));  // open: Qn, preset, en, reset
  D_Flip_Flop d_ff_2 (.clk(multiplexer_2_out), .D(or_3_out), .Q(\output [3]));  // open: Qn, preset, en, reset
  D_Flip_Flop d_ff_3 (.clk(multiplexer_2_out), .D(or_4_out), .Q(\output [2]));  // open: Qn, preset, en, reset
  D_Flip_Flop d_ff_4 (.clk(multiplexer_2_out), .D(or_5_out), .Q(\output [1]));  // open: Qn, preset, en, reset
  D_Flip_Flop d_ff_5 (.clk(multiplexer_2_out), .D(or_1_out), .Q(\output [0]));  // open: Qn, preset, en, reset

  // Other names for the same wires on the sheet: q0 = \output [0]; q1 = \output [1]; q2 = \output [2];
  //   q3 = \output [3]; q4 = \output [4]
endmodule
